// Logisim project CPU-DESIGN.circ as structural Verilog: 4 circuits, main circuit ALU
module ALU (
  input  [3:0] A,
  input  [3:0] B,
  input  [1:0] OP,
  output [3:0] OU
);

  wire [3:0] adder_1_out, and_1_out, or_1_out, xor_1_out;

  Adder #(.width(4)) adder_1 (.a(A), .b(B), .out(adder_1_out), .cin(1'b0));  // open: cout
  assign and_1_out = A & B;  // AND_Gate and_1, 4 bits wide
  assign or_1_out = A | B;  // OR_Gate or_1, 4 bits wide
  assign xor_1_out = A ^ B;  // XOR_Gate xor_1, 4 bits wide
  Multiplexer #(.select(2), .width(4)) multiplexer_1 (
    .in0(adder_1_out), .in1(and_1_out), .in2(or_1_out), .in3(xor_1_out), .out(OU), .sel(OP));
endmodule

module RE (
  input  [3:0] INP,
  input  CLK,
  input  [2:0] RA,
  input  [2:0] RD,
  input  [2:0] RB,
  output [3:0] A,
  output [3:0] B
);

  wire demultiplexer_1_out0, demultiplexer_1_out1, demultiplexer_1_out2, demultiplexer_1_out3,
       demultiplexer_1_out4, demultiplexer_1_out5, demultiplexer_1_out6, demultiplexer_1_out7;
  wire [3:0] R0_q, R1_q, R2_q, R3_q, R4_q, R5_q, R6_q, R7_q;

  Demultiplexer #(.select(3)) demultiplexer_1 (
    .out0(demultiplexer_1_out0), .out1(demultiplexer_1_out1), .out2(demultiplexer_1_out2),
    .out3(demultiplexer_1_out3), .out4(demultiplexer_1_out4), .out5(demultiplexer_1_out5),
    .out6(demultiplexer_1_out6), .out7(demultiplexer_1_out7), .in(1'b1), .sel(RD));
  Register #(.width(4)) R0 (.D(INP), .en(demultiplexer_1_out0), .clk(CLK), .Q(R0_q));  // open: clr
  Register #(.width(4)) R1 (.D(INP), .en(demultiplexer_1_out1), .clk(CLK), .Q(R1_q));  // open: clr
  Register #(.width(4)) R2 (.D(INP), .en(demultiplexer_1_out2), .clk(CLK), .Q(R2_q));  // open: clr
  Register #(.width(4)) R3 (.D(INP), .en(demultiplexer_1_out3), .clk(CLK), .Q(R3_q));  // open: clr
  Register #(.width(4)) R4 (.D(INP), .en(demultiplexer_1_out4), .clk(CLK), .Q(R4_q));  // open: clr
  Register #(.width(4)) R5 (.D(INP), .en(demultiplexer_1_out5), .clk(CLK), .Q(R5_q));  // open: clr
  Register #(.width(4)) R6 (.D(INP), .en(demultiplexer_1_out6), .clk(CLK), .Q(R6_q));  // open: clr
  Register #(.width(4)) R7 (.D(INP), .en(demultiplexer_1_out7), .clk(CLK), .Q(R7_q));  // open: clr
  Multiplexer #(.select(3), .width(4)) multiplexer_1 (
    .in0(R0_q), .in1(R1_q), .in2(R2_q), .in3(R3_q), .in4(R4_q), .in5(R5_q), .in6(R6_q), .in7(R7_q), .out(A),
    .sel(RA));
  Multiplexer #(.select(3), .width(4)) multiplexer_2 (
    .in0(R0_q), .in1(R1_q), .in2(R2_q), .in3(R3_q), .in4(R4_q), .in5(R5_q), .in6(R6_q), .in7(R7_q), .out(B),
    .sel(RB));
endmodule

module ALUSUB (
  input  [3:0] A,
  input  [3:0] B,
  input  [2:0] OP1,
  output Carry,
  output [3:0] OU1
);

  wire adder_1_cout, subtractor_1_bout;
  wire [3:0] adder_1_out, and_1_out, or_1_out, subtractor_1_out, xor_1_out;

  Adder #(.width(4)) adder_1 (.a(A), .b(B), .out(adder_1_out), .cin(1'b0), .cout(adder_1_cout));
  assign and_1_out = A & B;  // AND_Gate and_1, 4 bits wide
  Subtractor #(.width(4)) subtractor_1 (.a(A), .b(B), .out(subtractor_1_out), .bin(1'b0), .bout(subtractor_1_bout));
  assign or_1_out = A | B;  // OR_Gate or_1, 4 bits wide
  assign xor_1_out = A ^ B;  // XOR_Gate xor_1, 4 bits wide
  Multiplexer #(.select(3), .width(4)) multiplexer_1 (
    .in0(adder_1_out), .in1(and_1_out), .in2(subtractor_1_out), .in3(or_1_out), .in4(xor_1_out),
    .in5(4'b0000), .in6(4'b0000), .in7(4'b0000), .out(OU1), .sel(OP1));
  or or_2 (Carry, adder_1_cout, subtractor_1_bout);
endmodule

module mainsub (
);

  wire alusub_1_carry, CLK, DATA, MOV, nor_1_out, xor_1_out;
  wire [2:0] OP1, RA, RB, RD;
  wire [3:0] alusub_1_ou1, controlled_buffer_1_out, counter_1_q, counter_1_q_2, re_1_a, re_1_b;
  wire [15:0] rom_1_data;
  wire [15:9] register_1_q;

  Clock clock_1 (.out(CLK));
  Counter counter_1 (
    .clr(1'b0), .load(1'b0), .up(1'b1), .count(1'b1), .clk(CLK), .Q({counter_1_q_2, counter_1_q}));  // open: D, carry
  Hex_Digit_Display hex_digit_display_1 (.value(counter_1_q_2));  // open: dp
  Hex_Digit_Display hex_digit_display_2 (.value(counter_1_q));  // open: dp
  assign controlled_buffer_1_out = MOV ? {RB[0], RA} : 4'bz;  // Controlled_Buffer controlled_buffer_1
  ROM #(.dataWidth(16)) rom_1 (.addr({counter_1_q_2, counter_1_q}), .data(rom_1_data));
  assign controlled_buffer_1_out = DATA ? alusub_1_ou1 : 4'bz;  // Controlled_Buffer controlled_buffer_2
  RE re_1 (.INP(controlled_buffer_1_out), .CLK(CLK), .RA(RA), .RD(RD), .RB(RB), .A(re_1_a), .B(re_1_b));
  Register #(.width(16)) register_1 (
    .D(rom_1_data), .en(1'b1), .clk(CLK),
    .Q({register_1_q[15:14], OP1[1:0], OP1[2], register_1_q[10:9], RB, RA, RD}));  // open: clr
  ALUSUB alusub_1 (.A(re_1_a), .B(re_1_b), .OP1(OP1), .Carry(alusub_1_carry), .OU1(alusub_1_ou1));
  and and_1 (MOV, register_1_q[14], register_1_q[15]);
  and and_2 (DATA, ~register_1_q[14], ~register_1_q[15]);  // AND_Gate
  nor nor_1 (nor_1_out, alusub_1_ou1[3], alusub_1_ou1[2], alusub_1_ou1[1], alusub_1_ou1[0]);
  LED zero (.in(nor_1_out));
  LED negative (.in(alusub_1_ou1[3]));
  xor xor_1 (xor_1_out, alusub_1_ou1[3], alusub_1_ou1[2]);
  LED over_flow (.in(xor_1_out));
  LED carry (.in(alusub_1_carry));

  // Other names for the same wires on the sheet: VAL[3:0] = {RB[0], RA}

  // Notes on the sheet:
  //   contents of rom_1 (hex, n*v repeats v):
  //   c024 c02a 117 c043 c048 10ee 10ee
endmodule
