// Logisim project CPUII.circ as structural Verilog: 5 circuits, main circuit ALU
module main (
  output [3:0] out_1
);

  wire CLK, data, mov;
  wire [1:0] op;
  wire [2:0] RA, RB, RD;
  wire [3:0] controlled_buffer_1_out, counter_1_q, counter_1_q_2, registor_1_a, registor_1_b;
  wire [15:0] rom_1_data;
  wire [15:9] register_1_q;

  Clock clock_1 (.out(CLK));
  Counter counter_1 (
    .clr(1'b0), .load(1'b0), .up(1'b1), .count(1'b1), .clk(CLK), .Q({counter_1_q_2, counter_1_q}));  // open: D, carry
  assign controlled_buffer_1_out = mov ? {RA[0], RB} : 4'bz;  // Controlled_Buffer controlled_buffer_1
  Hex_Digit_Display hex_digit_display_1 (.value(counter_1_q_2));  // open: dp
  Hex_Digit_Display hex_digit_display_2 (.value(counter_1_q));  // open: dp
  ROM #(.dataWidth(16)) rom_1 (.addr({counter_1_q_2, counter_1_q}), .data(rom_1_data));
  assign controlled_buffer_1_out = data ? out_1 : 4'bz;  // Controlled_Buffer controlled_buffer_2
  REGISTOR registor_1 (
    .INP(controlled_buffer_1_out), .CLK(CLK), .RA(RA), .RD(RD), .RB(RB), .A(registor_1_a), .B(registor_1_b));
  Register #(.width(16)) register_1 (
    .D(rom_1_data), .en(1'b1), .clk(CLK), .Q({register_1_q[15:14], op, register_1_q[11:9], RA, RB, RD}));  // open: clr
  ALU alu_1 (.A(registor_1_a), .B(registor_1_b), .OP(op), .O(out_1));
  and and_1 (mov, register_1_q[14], register_1_q[15]);
  and and_2 (data, ~register_1_q[14], ~register_1_q[15]);  // AND_Gate

  // Other names for the same wires on the sheet: val[3:0] = {RA[0], RB}

  // Notes on the sheet:
  //   contents of rom_1 (hex, n*v repeats v):
  //   c04c c00d 312e c008 c011 a
endmodule

module ALU (
  input  [3:0] A,
  input  [3:0] B,
  input  [1:0] OP,
  output [3:0] O
);

  wire [3:0] adder_1_out, and_1_out, or_1_out, xor_1_out;

  Adder #(.width(4)) adder_1 (.a(A), .b(B), .out(adder_1_out), .cin(1'b0));  // open: cout
  assign and_1_out = A & B;  // AND_Gate and_1, 4 bits wide
  assign or_1_out = A | B;  // OR_Gate or_1, 4 bits wide
  assign xor_1_out = A ^ B;  // XOR_Gate xor_1, 4 bits wide
  Multiplexer #(.select(2), .width(4)) multiplexer_1 (
    .in0(adder_1_out), .in1(and_1_out), .in2(or_1_out), .in3(xor_1_out), .out(O), .sel(OP));
endmodule

module REGISTOR (
  input  [3:0] INP,
  input  CLK,
  input  [2:0] RA,
  input  [2:0] RD,
  input  [2:0] RB,
  output [3:0] A,
  output [3:0] B
);

  wire demultiplexer_1_out0, demultiplexer_1_out1, demultiplexer_1_out2, demultiplexer_1_out3,
       demultiplexer_1_out4, demultiplexer_1_out5, demultiplexer_1_out6, demultiplexer_1_out7;
  wire [3:0] R0_q, R1_q, R2_q, R3_q, R4_q, R5_q, R6_q, R7_q;

  Demultiplexer #(.select(3)) demultiplexer_1 (
    .out0(demultiplexer_1_out0), .out1(demultiplexer_1_out1), .out2(demultiplexer_1_out2),
    .out3(demultiplexer_1_out3), .out4(demultiplexer_1_out4), .out5(demultiplexer_1_out5),
    .out6(demultiplexer_1_out6), .out7(demultiplexer_1_out7), .in(1'b1), .sel(RD));
  Register #(.width(4)) R0 (.D(INP), .en(demultiplexer_1_out0), .clk(CLK), .Q(R0_q));  // open: clr
  Register #(.width(4)) R1 (.D(INP), .en(demultiplexer_1_out1), .clk(CLK), .Q(R1_q));  // open: clr
  Register #(.width(4)) R2 (.D(INP), .en(demultiplexer_1_out2), .clk(CLK), .Q(R2_q));  // open: clr
  Register #(.width(4)) R3 (.D(INP), .en(demultiplexer_1_out3), .clk(CLK), .Q(R3_q));  // open: clr
  Register #(.width(4)) R4 (.D(INP), .en(demultiplexer_1_out4), .clk(CLK), .Q(R4_q));  // open: clr
  Register #(.width(4)) R5 (.D(INP), .en(demultiplexer_1_out5), .clk(CLK), .Q(R5_q));  // open: clr
  Register #(.width(4)) R6 (.D(INP), .en(demultiplexer_1_out6), .clk(CLK), .Q(R6_q));  // open: clr
  Register #(.width(4)) R7 (.D(INP), .en(demultiplexer_1_out7), .clk(CLK), .Q(R7_q));  // open: clr
  Multiplexer #(.select(3), .width(4)) multiplexer_1 (
    .in0(R0_q), .in1(R1_q), .in2(R2_q), .in3(R3_q), .in4(R4_q), .in5(R5_q), .in6(R6_q), .in7(R7_q), .out(A),
    .sel(RA));
  Multiplexer #(.select(3), .width(4)) multiplexer_2 (
    .in0(R0_q), .in1(R1_q), .in2(R2_q), .in3(R3_q), .in4(R4_q), .in5(R5_q), .in6(R6_q), .in7(R7_q), .out(B),
    .sel(RB));
endmodule

module ALU2 (
  input  [3:0] A,
  input  [3:0] B,
  input  [2:0] OP,
  output Carry,
  output [3:0] O
);

  wire adder_1_cout, subtractor_1_bout;
  wire [3:0] adder_1_out, and_1_out, or_1_out, subtractor_1_out, xor_1_out;

  Adder #(.width(4)) adder_1 (.a(A), .b(B), .out(adder_1_out), .cin(1'b0), .cout(adder_1_cout));
  assign and_1_out = A & B;  // AND_Gate and_1, 4 bits wide
  assign or_1_out = A | B;  // OR_Gate or_1, 4 bits wide
  assign xor_1_out = A ^ B;  // XOR_Gate xor_1, 4 bits wide
  Subtractor #(.width(4)) subtractor_1 (.a(A), .b(B), .out(subtractor_1_out), .bin(1'b0), .bout(subtractor_1_bout));
  Multiplexer #(.select(3), .width(4)) multiplexer_1 (
    .in0(adder_1_out), .in1(and_1_out), .in2(or_1_out), .in3(xor_1_out), .in4(subtractor_1_out),
    .in5(4'b0000), .in6(4'b0000), .in7(4'b0000), .out(O), .sel(OP));
  or or_2 (Carry, adder_1_cout, subtractor_1_bout);
endmodule

module main2 (
);

  wire alu2_1_carry, CLK, data, mov, nor_1_out, xor_1_out;
  wire [2:0] op, RA, RB, RD;
  wire [3:0] alu2_1_o, controlled_buffer_1_out, counter_1_q, counter_1_q_2, registor_1_a, registor_1_b;
  wire [15:0] rom_1_data;
  wire [15:9] register_1_q;

  Counter counter_1 (
    .clr(1'b0), .load(1'b0), .up(1'b1), .count(1'b1), .clk(CLK), .Q({counter_1_q_2, counter_1_q}));  // open: D, carry
  assign controlled_buffer_1_out = mov ? {RA[0], RB} : 4'bz;  // Controlled_Buffer controlled_buffer_1
  Hex_Digit_Display hex_digit_display_1 (.value(counter_1_q_2));  // open: dp
  Hex_Digit_Display hex_digit_display_2 (.value(counter_1_q));  // open: dp
  ROM #(.dataWidth(16)) rom_1 (.addr({counter_1_q_2, counter_1_q}), .data(rom_1_data));
  assign controlled_buffer_1_out = data ? alu2_1_o : 4'bz;  // Controlled_Buffer controlled_buffer_2
  REGISTOR registor_1 (
    .INP(controlled_buffer_1_out), .CLK(CLK), .RA(RA), .RD(RD), .RB(RB), .A(registor_1_a), .B(registor_1_b));
  Clock clock_1 (.out(CLK));
  Register #(.width(16)) register_1 (
    .D(rom_1_data), .en(1'b1), .clk(CLK), .Q({register_1_q[15:14], op, register_1_q[10:9], RA, RB, RD}));  // open: clr
  ALU2 alu2_1 (.A(registor_1_a), .B(registor_1_b), .OP(op), .Carry(alu2_1_carry), .O(alu2_1_o));
  and and_1 (mov, register_1_q[14], register_1_q[15]);
  and and_2 (data, ~register_1_q[14], ~register_1_q[15]);  // AND_Gate
  nor nor_1 (nor_1_out, alu2_1_o[3], alu2_1_o[2], alu2_1_o[1], alu2_1_o[0]);
  LED zero (.in(nor_1_out));
  LED negative (.in(alu2_1_o[3]));
  xor xor_1 (xor_1_out, alu2_1_o[3], alu2_1_o[2]);
  LED over_flow (.in(xor_1_out));
  LED carry (.in(alu2_1_carry));

  // Other names for the same wires on the sheet: val[3:0] = {RA[0], RB}

  // Notes on the sheet:
  //   contents of rom_1 (hex, n*v repeats v):
  //   c019 c012 54 53 2056 0 c008 c03c 2107
endmodule
